# Fritzing sketch LCD_I2C (saved by Fritzing 1.0.4)

parts:
  Arduino = Arduino Uno (Rev3)
  Bauteil1 = LCD1602-I2C

nets:
  GND: Arduino.GND, Bauteil1.GND
  N1: Arduino.A4/SDA, Bauteil1.SDA
  N2: Arduino.A5/SCL, Bauteil1.SCL
  5V: Arduino.5V, Bauteil1.VCC

custom parts:
  LCD1602-I2C: A standard character display, usually with 2x16 characters. Comes in many colors with LCM1602 IIC attached.
